# Fritzing sketch schematic (saved by Fritzing 0.9.3b)

parts:
  Componente1 = BH1750
  Raspberry_Pi_1 = Raspberry Pi 3 [part_number=RPI-3-V1.2]

nets:
  VCC: Componente1.VCC, Raspberry_Pi_1.3v3
  GND: Componente1.GND, Raspberry_Pi_1.GND
  N1: Componente1.SCL, Raspberry_Pi_1.GPIO3
  N2: Componente1.SDA, Raspberry_Pi_1.GPIO2

custom parts:
  BH1750: Light Sensor
